# Fritzing sketch Digital Control System Schematic (saved by Fritzing 0.9.10b)

parts:
  U2 = ESP8266 NodeMCU LoLin module
  THERMO1 = MAX31855 Breakout Board with Thermocouple
  OLED_I2C1 = OLED 128x64 I2C Monochrome Display
  IC1 = ULN2803A [package=THT]
  BAT1 = 12 battery [package=battery]
  D1 = Rectifier Diode [part_number=1N4004 package="Melf DO-213 AB [SMD]"]
  U4 = 941H-2C-5D [package=relay-5v]

nets:
  N1: U2.D0, THERMO1.CLK
  N2: U2.D1, OLED_I2C1.SCK
  N3: U2.D2, OLED_I2C1.SDA
  N4: U2.D3, THERMO1.CS
  N5: U2.D4, THERMO1.DO
  GND: U2.GND, THERMO1.GND, OLED_I2C1.GND, IC1.0V, BAT1.-, U4.13
  N6: U2.D8, IC1.In_4
  VIN: U2.Vin, OLED_I2C1.VDD
  N7: IC1.COM_-_Common, BAT1.+, D1.cathode, U4.1, U4.4
  N8: IC1.Out_4, D1.anode, U4.16

notes:
  The thermocouple module that was used for the Digital Control System does not have a fritzing file, but it should look similar to this
  To Oven
  20 AH

custom parts:
  ESP8266 NodeMCU LoLin module: ESP8266 based NodeMCU
  12 battery: 12V lead acid type battery, like the Husqvarna YTH2448 12V 35AH battery. The pads in pcb are sized to accomidate up to 14ga wire (as these batterys will deliver high currents.)
  941H-2C-5D: DPDT Relay - 2 Form C
